// Logisim project TASK2.circ as structural Verilog: 1 circuit, main circuit main
module main (
  input  A,
  input  B,
  input  C,
  output SUM,
  output C_out
);

  wire AND_2_out, AND_3_out, AND_out;

  xor XOR (SUM, A, B, C);
  and AND (AND_out, A, B);
  and AND_2 (AND_2_out, A, C);
  and AND_3 (AND_3_out, B, C);
  or or_1 (C_out, AND_out, AND_2_out, AND_3_out);
endmodule
