// Logisim project TASK4.circ as structural Verilog: 1 circuit, main circuit main
module main (
  input  A3,
  input  A2,
  input  D_in,
  input  A1,
  input  A0,
  input  E,
  input  [1:0] S,
  input  [1:0] S_2,
  input  E_2,
  input  A7,
  input  A6,
  input  A5,
  input  A4,
  input  A3_2,
  input  D_in_2,
  input  A2_2,
  input  A1_2,
  input  A0_2,
  input  [2:0] S_3,
  input  E_3,
  input  E_4,
  input  [2:0] S_4,
  output Y0,
  output Y1,
  output Y2,
  output Y,
  output Y3,
  output Y0_2,
  output Y1_2,
  output Y2_2,
  output Y3_2,
  output Y_2,
  output Y4,
  output Y5,
  output Y6,
  output Y7
);

  Multiplexer #(.select(2)) multiplexer_1 (.in0(A3), .in1(A2), .in2(A1), .in3(A0), .out(Y), .sel(S_2), .en(E_2));
  Multiplexer #(.select(3)) multiplexer_2 (
    .in0(A7), .in1(A6), .in2(A5), .in3(A4), .in4(A3_2), .in5(A2_2), .in6(A1_2), .in7(A0_2), .out(Y_2),
    .sel(S_3), .en(E_3));
  Demultiplexer #(.select(2)) demultiplexer_1 (.out0(Y0), .out1(Y1), .out2(Y2), .out3(Y3), .in(D_in), .sel(S), .en(E));
  Demultiplexer #(.select(3)) demultiplexer_2 (
    .out0(Y0_2), .out1(Y1_2), .out2(Y2_2), .out3(Y3_2), .out4(Y4), .out5(Y5), .out6(Y6), .out7(Y7),
    .in(D_in_2), .sel(S_4), .en(E_4));

  // Notes on the sheet:
  //   4x1 Multiplexer
  //   8x1 Multiplexer
  //   1:4 Demultiplexer
  //   1:8 Demultiplexer
endmodule
