// Logisim project TASK5.circ as structural Verilog: 1 circuit, main circuit main
module main (
  input  [3:0] in_1,
  input  in_2,
  input  in_3,
  input  in_4,
  input  in_5,
  input  in_6,
  output [3:0] out_7
);

  wire [3:0] ram_1_data, rom_1_data;

  RAM #(.addrWidth(4), .dataWidth(4)) ram_1 (
    .addr(in_1), .data(ram_1_data), .sel(in_2), .ld(in_3), .clr(in_4));  // open: clk
  ROM #(.addrWidth(4), .dataWidth(4)) rom_1 (.addr(in_1), .data(rom_1_data), .sel(in_6));
  Multiplexer #(.width(4), .enable("false")) multiplexer_1 (
    .in0(ram_1_data), .in1(rom_1_data), .out(out_7), .sel(in_5));

  // Notes on the sheet:
  //   MEMORY BASED SYSTEM
  //   contents of rom_1 (hex, n*v repeats v):
  //   a 4*0 b 0 0 0 c 4*0 d
endmodule
