// Logisim project TASK-2.circ as structural Verilog
module BCD (
  input  A,
  input  B,
  input  C,
  input  D,
  output A_2,
  output B_2,
  output C_2,
  output D_2,
  output E,
  output F,
  output G
);

  wire and_1_out, and_2_out, and_3_out, and_4_out, and_5_out, and_6_out, and_7_out, and_8_out, and_9_out,
       and_10_out, and_11_out, and_12_out, and_13_out, and_14_out, and_15_out, and_16_out, not_1_out,
       not_2_out, not_3_out, not_4_out, not_5_out, not_6_out, not_7_out, not_8_out, not_9_out, not_10_out,
       not_11_out, not_12_out, not_13_out, not_14_out, not_15_out, not_16_out, not_17_out, not_18_out,
       not_19_out, not_20_out, not_21_out;

  not not_1 (not_1_out, B);
  and and_1 (and_1_out, not_1_out, not_2_out);
  not not_2 (not_2_out, D);
  and and_2 (and_2_out, B, D);
  not not_3 (not_3_out, B);
  not not_4 (not_4_out, C);
  and and_3 (and_3_out, not_4_out, not_5_out);
  not not_5 (not_5_out, D);
  and and_4 (and_4_out, C, D);
  not not_6 (not_6_out, C);
  or or_1 (C_2, not_6_out, D, B);
  not not_7 (not_7_out, B);
  and and_5 (and_5_out, not_7_out, not_8_out);
  not not_8 (not_8_out, D);
  not not_9 (not_9_out, B);
  and and_6 (and_6_out, not_9_out, C);
  and and_7 (and_7_out, C, not_10_out);
  not not_10 (not_10_out, D);
  and and_8 (and_8_out, B, not_11_out, D);
  not not_11 (not_11_out, C);
  not not_12 (not_12_out, B);
  and and_9 (and_9_out, not_12_out, not_13_out);
  not not_13 (not_13_out, D);
  and and_10 (and_10_out, C, not_14_out);
  not not_14 (not_14_out, D);
  not not_15 (not_15_out, C);
  and and_11 (and_11_out, not_15_out, not_16_out);
  not not_16 (not_16_out, D);
  and and_12 (and_12_out, B, not_17_out);
  not not_17 (not_17_out, C);
  and and_13 (and_13_out, B, not_18_out);
  not not_18 (not_18_out, D);
  not not_19 (not_19_out, B);
  and and_14 (and_14_out, not_19_out, C);
  and and_15 (and_15_out, B, not_20_out);
  not not_20 (not_20_out, C);
  and and_16 (and_16_out, B, not_21_out);
  not not_21 (not_21_out, D);
  or or_2 (A_2, and_1_out, C, and_2_out, A);
  or or_3 (B_2, not_3_out, and_3_out, and_4_out);
  or or_4 (D_2, and_5_out, and_6_out, and_7_out, and_8_out, A);
  or or_5 (E, and_9_out, and_10_out);
  or or_6 (F, and_11_out, and_12_out, and_13_out, A);
  or or_7 (G, and_14_out, and_15_out, and_16_out, A);
endmodule

module BCD_7SEGMENT (
  input  in_1,
  input  in_2,
  input  in_3,
  input  in_4
);

  wire bcd_1_a_2, bcd_1_b_2, bcd_1_c_2, bcd_1_d_2, bcd_1_e, bcd_1_f, bcd_1_g;

  BCD bcd_1 (
    .A(in_4), .B(in_3), .C(in_2), .D(in_1), .A_2(bcd_1_a_2), .B_2(bcd_1_b_2), .C_2(bcd_1_c_2),
    .D_2(bcd_1_d_2), .E(bcd_1_e), .F(bcd_1_f), .G(bcd_1_g));
  _7_Segment_Display u_7_segment_display_1 (
    .g(bcd_1_g), .f(bcd_1_f), .a(bcd_1_a_2), .b(bcd_1_b_2), .e(bcd_1_e), .d(bcd_1_d_2), .c(bcd_1_c_2));  // open: dp
endmodule

module _1_BIT_ALU (
  input  INPUT_A,
  input  INPUT_B,
  input  Cin,
  input  [2:0] S0_S1_S2,
  output SUM,
  output CARRY
);

  wire adder_1_cout, adder_1_out, and_1_out, multiplier_1_cout, multiplier_1_out, or_1_out,
       subtractor_1_bout, subtractor_1_out, xor_1_out;

  and and_1 (and_1_out, INPUT_A, INPUT_B);
  or or_1 (or_1_out, INPUT_A, INPUT_B);
  Adder #(.width(1)) adder_1 (.a(INPUT_A), .b(INPUT_B), .out(adder_1_out), .cin(Cin), .cout(adder_1_cout));
  Subtractor #(.width(1)) subtractor_1 (
    .a(INPUT_A), .b(INPUT_B), .out(subtractor_1_out), .bin(Cin), .bout(subtractor_1_bout));
  Multiplier #(.width(1)) multiplier_1 (
    .a(INPUT_A), .b(INPUT_B), .out(multiplier_1_out), .cin(Cin), .cout(multiplier_1_cout));
  xor xor_1 (xor_1_out, INPUT_A, INPUT_B);
  Multiplexer #(.select(3)) multiplexer_1 (
    .in0(and_1_out), .in1(or_1_out), .in2(xor_1_out), .in3(adder_1_out), .in4(subtractor_1_out),
    .in5(multiplier_1_out), .out(SUM), .sel(S0_S1_S2));  // open: in6, in7, en
  Multiplexer #(.select(3)) multiplexer_2 (
    .in3(adder_1_cout), .in4(subtractor_1_bout), .in5(multiplier_1_cout), .out(CARRY), .sel(S0_S1_S2));  // open: in0, in1, in2, in6, in7, en
endmodule

module _4_BIT_ALU (
  input  [2:0] in_1,
  input  Cin,
  input  B3,
  input  B2,
  input  B1,
  input  B_0,
  input  A3,
  input  A2,
  input  A1,
  input  A0,
  output out_11,
  output out_12,
  output out_13,
  output out_14,
  output out_15
);

  wire n1_bit_alu_1_carry, n1_bit_alu_2_carry, n1_bit_alu_3_carry;

  _1_BIT_ALU u_1_bit_alu_1 (
    .INPUT_A(A0), .INPUT_B(B_0), .Cin(Cin), .S0_S1_S2(in_1), .SUM(out_11), .CARRY(n1_bit_alu_1_carry));
  _1_BIT_ALU u_1_bit_alu_2 (
    .INPUT_A(A1), .INPUT_B(B1), .Cin(n1_bit_alu_1_carry), .S0_S1_S2(in_1), .SUM(out_12),
    .CARRY(n1_bit_alu_2_carry));
  _1_BIT_ALU u_1_bit_alu_3 (
    .INPUT_A(A2), .INPUT_B(B2), .Cin(n1_bit_alu_2_carry), .S0_S1_S2(in_1), .SUM(out_13),
    .CARRY(n1_bit_alu_3_carry));
  _1_BIT_ALU u_1_bit_alu_4 (
    .INPUT_A(A3), .INPUT_B(B3), .Cin(n1_bit_alu_3_carry), .S0_S1_S2(in_1), .SUM(out_14), .CARRY(out_15));
endmodule
